# Fritzing sketch ölçü_aleti (saved by Fritzing 0.9.3b)
breadboards: 1

parts:
  Parça1 = Arduino Uno (Rev3)
  LCD1 = LCD screen
  RE1 = Rotary Encoder [package=THT]
  S2 = Round Pushbutton
  S3 = Round Pushbutton
  S4 = Round Pushbutton
  R2 = Resistor [tolerance=±5% resistance=220 package=THT]
  R3 = Resistor [tolerance=±5% resistance=220 package=THT]
  R4 = Resistor [tolerance=±5% resistance=220 package=THT]
  R6 = Resistor [tolerance=±5% resistance=220 package=THT]
  R7 = Trimmer Potentiometer [maximum_resistance=10kΩ package=THT]  # not connected
  R9 = Resistor [tolerance=±5% resistance=10k package="0402 [SMD]"]
  R10 = Resistor [tolerance=±5% resistance=10k package="0402 [SMD]"]
  R11 = Resistor [tolerance=±5% resistance=220 package=THT]  # not connected
  C1 = Electrolytic Capacitor [capacitance=1µF package="100 mil [THT, electrolytic]"]  # not connected

nets:
  N1: Parça1.A1, R9.Pin_0
  N2: Parça1.A3, R6.Pin_0, R10.Pin_0
  N3: Parça1.D8, LCD1.RS
  N4: Parça1.D9_PWM, LCD1.E
  N5: Parça1.D11_PWM/MOSI, R6.Pin_1, R10.Pin_1
  N6: Parça1.D4, LCD1.DB4
  N7: Parça1.D5_PWM, LCD1.DB5
  N8: Parça1.D6_PWM, LCD1.DB6
  N9: Parça1.D7, LCD1.DB7
  N10: LCD1.VSS, RE1.EncoderPinB
  N11: LCD1.VDD, RE1.EncoderPinA
  N12: LCD1.V0, RE1.EncoderPinC
  N13: S2.leg0, R4.Pin_0
  N14: S3.leg0, R3.Pin_0
  N15: S4.leg0, R2.Pin_0
