# Fritzing sketch Arduino_Uno_i2C_LCD (saved by Fritzing 0.9.3b)
breadboards: 1

parts:
  Onderdeel1 = Arduino Uno (Rev3)
  BREAKOUT2 = ULN2003A breakout board
  hc-sr2 = hc-sr04
  J2 = Piezo Speaker
  Parça4 = DeuLigne 1.1 - The Snootlab's LCD shield for Arduino
  M3 = Stepper Motor - Bipolar  # not connected
  LCM1602_IIC2 = LCM1602 IIC [part_number="LCM1602 IIC" chip_label="LCM1602 IIC" package="DIP (Dual Inline) [THT]"]
  R1 = Resistor [tolerance=±5% resistance=220 package=THT]

nets:
  N1: Onderdeel1.D8, hc-sr2.Trig
  N2: Onderdeel1.D9_PWM, hc-sr2.Echo
  N3: Onderdeel1.A4/SDA, LCM1602_IIC2.SDA
  N4: Onderdeel1.A5/SCL, LCM1602_IIC2.SCL
  N5: Onderdeel1.D2, BREAKOUT2.In_1
  N6: Onderdeel1.D3_PWM, BREAKOUT2.In_2
  N7: Onderdeel1.D4, BREAKOUT2.In_3
  N8: Onderdeel1.D5_PWM, BREAKOUT2.In_4
  N9: Onderdeel1.D6_PWM, R1.Pin_1
  5V: Onderdeel1.5V, BREAKOUT2.+5V, LCM1602_IIC2.VCC
  GND: Onderdeel1.GND, BREAKOUT2.0V, J2.pin1, LCM1602_IIC2.GND
  N10: Parça4.D8, LCM1602_IIC2.D6
  N11: Parça4.D9, LCM1602_IIC2.D4
  N12: Parça4.D4, LCM1602_IIC2.E
  N13: Parça4.D5, LCM1602_IIC2.RW
  N14: Parça4.D6, LCM1602_IIC2.RS
  N15: Parça4.D7, LCM1602_IIC2.V0
  N16: Parça4.+5V, LCM1602_IIC2.A
  N17: Parça4.GND, LCM1602_IIC2.K

notes:
  HALİL GÖK
  The Engineers

custom parts:
  ULN2003A breakout board: ULN2003A 7-way Darlington Transistor Driver on breakoutboard
  LCM1602 IIC: I2C-Module to use a 1602 or 2004 LCD on with the wire.h libory Serial LCD Modul

// code stored in the sketch: AnalogReadSerial2LCD_LED.ino
#include <Wire.h>
#include <LiquidCrystal_I2C.h>

LiquidCrystal_I2C lcd(0x27, 16, 2);   // adress and format LCD

const int analogInPin = A0;           // Analog input pin that the potentiometer is attached to
const int analogOutPin = 9;           // Analog output pin that the LED is attached to

int sensorValue = 0;                  // value read from the pot
int outputValue = 0;                  // value output to the PWM (analog out)

void setup() {
  lcd.init();                         // init LCD
  lcd.backlight();
  lcd.home();
  lcd.setCursor(5, 0);                // place static text
  lcd.print("ADC = ");
  lcd.setCursor(15, 0);
  lcd.print("V");
  lcd.setCursor(0, 1);
  lcd.print("LED : ");
  lcd.setCursor(12, 1);
  lcd.print("%");
  Serial.begin(9600);                 // optional serial monitor
}

void loop() {
  int sensorValue = analogRead(analogInPin);          // read analog A0 en store in sensorValue
  float voltValue = 5.0 / 1024.0 * sensorValue;       // calculate volt at analog A0 and store in voltValue
  float percentValue = sensorValue / 1024.0 * 100.0;  // calculate percentage analog A0 and store in percentValue
  outputValue = map(sensorValue, 0, 1023, 0, 255);    // map analog input to analog output and store in outputValue
  analogWrite(analogOutPin, outputValue);             // write outputValue to analogOutPin

  lcd.setCursor(0, 0);                                // set cursor at deserid position
  leadingZeros(sensorValue, 4);                       // print sensorvalue with number of leading-characters (0 or space as specified in function leadingZeros)
  lcd.setCursor(10, 0);                               // set cursor at deserid position
  lcd.print(voltValue);                               // print voltValue
  lcd.setCursor(6, 1);                                // set cursor at deserid position
  lcd.print(percentValue);                            // print percentValue

  Serial.print("sensor = " );                         // print the results to the serial monitor:
  Serial.print(sensorValue);
  Serial.print("\t output = ");
  Serial.print(outputValue);
  Serial.print("\t procent = ");
  Serial.println(percentValue);

  delay(1000);                                        // set delay
}

void leadingZeros( int value, int width) {            // display result with leading characters
  char valueStr[6];                                   // large enough to hold an int
  itoa (value, valueStr, 10);                         // itoa converts int to string
  int len = strlen(valueStr);                         // calculate length of valueStr
  if (len < width) {
    len = width - len;
    while (len--)
      lcd.print(' ');                                 // for leading zeros place '0' between (), for leading spaces place ' ' between ()
  }
  lcd.print(valueStr);
}
